# Fritzing sketch Controller (saved by Fritzing 0.9.3b)
circuit board: 11.9279cm x 8.23392cm
perfboards: 1

parts:
  Part1 = Arduino Uno (Rev3)
  R5 = Temperature Sensor (Thermistor) [thermistor_type=NTC package=THT]
  R6 = Resistor [tolerance=±5% resistance=10k package=THT]
  R7 = Resistor [tolerance=±5% resistance=10k package=THT]
  R8 = Temperature Sensor (Thermistor) [thermistor_type=NTC package=THT]

nets:
  N1: Part1.A3, R6.Pin_1, R8.pin_0
  N2: Part1.A4/SDA, R5.pin_1, R7.Pin_1
  N3: Part1.AREF, Part1.3V3, R6.Pin_0, R7.Pin_0
  N4: Part1.GND, R8.pin_1
