# Fritzing sketch buttonPad (saved by Fritzing 0.9.3b)
perfboards: 1

parts:
  HC165 = IC, DIP package, 16 pins [chip_label=IC]
  J1 = female pin header, 5 pins [form="♀ (female)"]
  Btn1 = female pin header, 2 pins [form="♀ (female)"]
  Btn2 = female pin header, 2 pins [form="♀ (female)"]
  Btn3 = female pin header, 2 pins [form="♀ (female)"]
  Btn4 = female pin header, 2 pins [form="♀ (female)"]
  Btn5 = female pin header, 2 pins [form="♀ (female)"]
  Btn6 = female pin header, 2 pins [form="♀ (female)"]
  Btn7 = female pin header, 2 pins [form="♀ (female)"]
  Btn8 = female pin header, 2 pins [form="♀ (female)"]
  R1 = Resistor [tolerance=±5% resistance=220 package=THT]
  R2 = Resistor [tolerance=±5% resistance=220 package=THT]
  R3 = Resistor [tolerance=±5% resistance=220 package=THT]
  R4 = Resistor [tolerance=±5% resistance=220 package=THT]
  R5 = Resistor [tolerance=±5% resistance=220 package=THT]
  R6 = Resistor [tolerance=±5% resistance=220 package=THT]
  R7 = Resistor [tolerance=±5% resistance=220 package=THT]
  R8 = Resistor [tolerance=±5% resistance=220 package=THT]

nets:
  N1: HC165.pin1, J1.pin3
  N2: HC165.pin2, J1.pin4
  N3: HC165.pin3, Btn8.pin1, R8.Pin_1
  N4: HC165.pin4, Btn7.pin1, R7.Pin_1
  N5: HC165.pin5, Btn6.pin1, R6.Pin_1
  N6: HC165.pin6, Btn5.pin1, R5.Pin_1
  N7: HC165.pin8, HC165.pin15, J1.pin2, R1.Pin_1, R2.Pin_1, R3.Pin_1, R4.Pin_1, R5.Pin_0, R6.Pin_0, R7.Pin_0, R8.Pin_0
  N8: HC165.pin9, J1.pin5
  N9: HC165.pin11, Btn4.pin1, R4.Pin_0
  N10: HC165.pin12, Btn3.pin1, R3.Pin_0
  N11: HC165.pin13, Btn2.pin1, R2.Pin_0
  N12: HC165.pin14, Btn1.pin1, R1.Pin_0
  N13: J1.pin1, Btn1.pin2, Btn2.pin2, Btn3.pin2, Btn4.pin2, Btn5.pin2, Btn6.pin2, Btn7.pin2, Btn8.pin2
