# Fritzing sketch buttonPad1 (saved by Fritzing 0.9.3b)
circuit board: 8.46667cm x 5.64444cm
perfboards: 1

parts:
  J1 = female pin header, 5 pins [form="♀ (female)"]
  IC1 = IC, DIP package, 16 pins [chip_label=IC]
  Btn1 = Pushbutton [package=THT]
  R1 = Resistor [tolerance=±5% resistance=220 package=THT]
  R4 = Resistor [tolerance=±5% resistance=220 package=THT]
  Btn4 = Pushbutton [package=THT]
  R2 = Resistor [tolerance=±5% resistance=220 package=THT]
  Btn2 = Pushbutton [package=THT]
  Btn3 = Pushbutton [package=THT]
  R3 = Resistor [tolerance=±5% resistance=220 package=THT]
  Btn5 = Pushbutton [package=THT]
  Btn6 = Pushbutton [package=THT]
  Btn7 = Pushbutton [package=THT]
  Btn8 = Pushbutton [package=THT]
  R5 = Resistor [tolerance=±5% resistance=220 package=THT]
  R6 = Resistor [tolerance=±5% resistance=220 package=THT]
  R7 = Resistor [tolerance=±5% resistance=220 package=THT]
  R8 = Resistor [tolerance=±5% resistance=220 package=THT]

nets:
  N1: J1.pin1, Btn1.leg1, Btn4.leg1, Btn2.leg1, Btn3.leg1, Btn5.leg1, Btn6.leg1, Btn7.leg1, Btn8.leg1
  N2: J1.pin2, IC1.pin8, IC1.pin15, R1.Pin_1, R4.Pin_1, R2.Pin_1, R3.Pin_1, R5.Pin_0, R6.Pin_0, R7.Pin_0, R8.Pin_0
  N3: J1.pin3, IC1.pin1
  N4: J1.pin4, IC1.pin2
  N5: J1.pin5, IC1.pin9
  N6: IC1.pin3, Btn8.leg0, R8.Pin_1
  N7: IC1.pin4, Btn7.leg0, R7.Pin_1
  N8: IC1.pin5, Btn6.leg0, R6.Pin_1
  N9: IC1.pin6, Btn5.leg0, R5.Pin_1
  N10: IC1.pin11, Btn1.leg0, R1.Pin_0
  N11: IC1.pin12, R2.Pin_0, Btn2.leg0
  N12: IC1.pin13, Btn3.leg0, R3.Pin_0
  N13: IC1.pin14, R4.Pin_0, Btn4.leg0
